# Fritzing sketch meteo (saved by Fritzing 0.9.5d)
breadboards: 1

parts:
  WeMos_D1_R1 = WeMos D1 R2
  DS1 = DS18B20 1-Wire Temperature Sensor [part_number=DS18B20]
  R1 = Resistor [tolerance=±5% power=0.25 resistance=4.7k package=THT]
  Компонент1 = Barometric Pressure Sensor - BMP180 Breakout (GY-68)
  Компонент2 = Adafruit AHT20 Temperature and Humidity Sensor [part_number="Adafruit #4566"]

nets:
  N1: WeMos_D1_R1.D3, Компонент1.SCL, Компонент2.SCL
  N2: WeMos_D1_R1.D4, Компонент1.SDA, Компонент2.SDA
  N3: WeMos_D1_R1.D9, DS1.DQ, R1.Pin_1
  GND: WeMos_D1_R1.GND, DS1.GND, Компонент1.GND, Компонент2.GND
  VCC: WeMos_D1_R1.3.3V, DS1.VDD, R1.Pin_0, Компонент1.VCC, Компонент2.VCC

custom parts:
  WeMos D1 R2: The D1 R2 is a mini wifi board based on the ESP-8266EX.
  Adafruit AHT20 Temperature and Humidity Sensor: The AHT20 is a nice but inexpensive temperature and humidity sensor from the same folks that brought us the DHT22. You can take sensor readings as often as you like, and it uses standard I2C so its super easy to use with any Arduino or Linux/Raspberry Pi board. This sensor has a typical accuracy of +- 2% relative humidity, and +-0.3 °C. There is only one I2C address so its not a good option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
